# Fritzing sketch Lab 1 (saved by Fritzing 0.9.4)
breadboards: 1

parts:
  U1 = 7400 4 x 2 Input NAND Gate [part_number=7400 package="DIP (Dual Inline) [THT]"]
  R1 = Resistor [tolerance=±5% resistance=220 package="2512 [SMD]"]
  R2 = Resistor [tolerance=±5% resistance=220 package="2512 [SMD]"]
  D1 = LED_BARGRAPH_10 [package=led_bargaph_10]
  R4 = Resistor [tolerance=±5% resistance=220 package="2512 [SMD]"]
  R5 = Resistor [tolerance=±5% resistance=220 package=THT]
  R6 = Resistor [tolerance=±5% resistance=220 package=THT]
  R7 = Resistor [tolerance=±5% resistance=220 package=THT]
  SW1 = DIP Switch 8 Position [package=dipswitch-08]
  U2 = 7400 4 x 2 Input NAND Gate [part_number=7400 package="DIP (Dual Inline) [THT]"]
  J1 = Screw terminal - 2 pins [package=THT]

nets:
  A: U1.A1, D1.A_A, R5.Pin_1, SW1.1, U2.A1
  B: U1.B1, U1.Q2, U1.A2, D1.B_A, R6.Pin_1, SW1.2
  D= A NAND B: U1.Q1, U1.A4
  E = B NAND B: U1.B2, U1.B3
  N1: U1.GND, R5.Pin_0, R6.Pin_0, R7.Pin_0, J1.pin1
  F = C NAND E: U1.A3, U1.B4
  C: U1.Q3, R7.Pin_1, SW1.3, U2.B1
  Z: U1.Q4, D1.C_A, U2.Q2, U2.A2
  N2: U1.VDD, R1.Pin_1, R2.Pin_1, R4.Pin_1, SW1.14, SW1.15, SW1.16, J1.pin2
  N3: R1.Pin_0, D1.B_C
  N4: R2.Pin_0, D1.A_C
  N5: D1.F_A, U2.A3
  N6: D1.C_C, R4.Pin_0
  N7: U2.Q1, U2.B3
  N8: U2.B2, U2.Q3
