# Fritzing sketch Lab2 fritzing (saved by Fritzing 0.9.4)
breadboards: 3

parts:
  R10 = 1k Resistor [package=THT]
  U10 = 74153 Dual 4:1 MUX [part_number=74153 package="DIP16 [THT]"]
  R12 = 1k Resistor [package=THT]
  U7 = 7404 Hex Inverter [part_number=7404 package=dil14]
  JP1 = Header 11 [package=1x11_smd_no_holes]
  U6 = 7486 4 x 2 Input XOR Gate [part_number=7486 package="DIP (Dual Inline) [THT]"]
  R6 = 1k Resistor [package=THT]
  R1 = 1k Resistor [package=THT]
  R3 = 1k Resistor [package=THT]
  D1 = LED_BARGRAPH_10 [package=led_bargaph_10]
  R4 = 1k Resistor [package=THT]
  D4 = LED_BARGRAPH_10 [package=led_bargaph_10]
  U11 = 74157 Quad 2:1 MUX [part_number=74157 package="DIP16 [THT]"]
  U5 = 74161 4 Bit Synchronous Up Down Counter [part_number=74161 package="DIP16 [THT]"]
  U4 = 74194 4 Bit Bi-Directional Shift Register [part_number=74194 package="DIP16 [THT]"]
  U12 = 7474 Dual Positive Edge Triggered D Flip Flop [part_number=7474 package="DIP (Dual Inline) [THT]"]
  U3 = 74194 4 Bit Bi-Directional Shift Register [part_number=74194 package="DIP16 [THT]"]
  R7 = 1k Resistor [package=THT]
  D2 = LED_BARGRAPH_10 [package=led_bargaph_10]
  R2 = 1k Resistor [package=THT]
  R9 = 1k Resistor [package=THT]
  U8 = 7400 4 x 2 Input NAND Gate [part_number=7400 package="DIP (Dual Inline) [THT]"]
  R13 = 1k Resistor [package=THT]
  R11 = 1k Resistor [package=THT]
  D3 = LED_BARGRAPH_10 [package=led_bargaph_10]
  R14 = 1k Resistor [package=THT]
  R15 = 1k Resistor [package=THT]

nets:
  GND: R10.Pin_0, U10.G1, U10.G0, U10.GND, R12.Pin_0, U7.GND, U6.GND, R6.Pin_0, R1.Pin_0, R3.Pin_0, R4.Pin_0, U11.GND, U5.GND, U4.GND, U4.10, U12.GND, U3.GND, U3.10, R7.Pin_0, R2.Pin_0, R9.Pin_0, U8.GND, R13.Pin_0, R11.Pin_0, R14.Pin_0, R15.Pin_0
  N1: R10.Pin_1, D3.F_C
  DATA[0]: U10.D0, U10.C0, JP1.6
  DATA[1]: U10.C1, U10.D1, JP1.7
  N2: U10.Y1, U10.A1, U12.A4
  N3: U10.Y0, U12.B1
  4 to 1 MUX SB [1]/LOAD: U10.S1, JP1.4, D4.C_A
  N4: U10.B0, D1.F_A, U11.B0, U3.12
  N5: U10.B1, U11.B1, U4.12, D2.E_A
  4 to 1 MUX SB [0]: U10.S0, D4.B_A, U8.A3
  VCC: U10.VCC, U7.VCC, U6.VDD, U11.VCC, U5.1, U5.7, U5.10, U5.VCC, U4.9, U4.VCC, U12.A1, U12.Q2, U12.Q3, U12.B4, U12.VDD, U3.9, U3.VCC, U8.VDD
  N6: R12.Pin_1, D4.B_C
  N7: U7.1A, U6.Q1
  N8: U7.1Y, U8.A1
  N9: U7.2A, U6.B2
  N10: U7.2Y, U8.B1
  N11: U7.3A, U8.Q1
  N12: U7.3Y, U8.Q2
  2 to 1 MUX SB: U7.4Y, D4.A_A, U11.SEL
  N13: U7.4A, U8.B2, U8.Q3
  SAR[0]: JP1.1, U6.A1
  SAR[1]: JP1.2, U6.A2
  Store: JP1.3, U8.A2
  Fetch: JP1.5, U8.B3
  CLK: JP1.8, U5.2, U4.11, U12.Q1, U12.Q4, U3.11
  N14: U6.B1, U5.14
  N15: U6.Q2, U5.13
  N16: R6.Pin_1, D2.D_C
  N17: R1.Pin_1, D1.C_C
  N18: R3.Pin_1, D1.E_C
  N19: D1.C_A, U3.15
  N20: D1.D_A, U3.14
  N21: D1.E_A, U3.13
  N22: D1.F_C, R4.Pin_1
  N23: D1.D_C, R2.Pin_1
  N24: D4.C_C, R13.Pin_1
  N25: D4.A_C, R11.Pin_1
  N26: U11.Y0, U3.2
  N27: U11.Y1, U4.2
  N28: U11.A0, U12.A2, D3.F_A
  N29: U11.A1, U12.B3, D3.E_A
  N30: U4.13, D2.D_A
  N31: U4.14, D2.C_A
  N32: U4.15, D2.B_A
  N33: R7.Pin_1, D2.E_C
  N34: D2.C_C, R14.Pin_1
  N35: D2.B_C, R15.Pin_1
  N36: R9.Pin_1, D3.E_C

custom parts:
  1k Resistor: A generic 5-band resistor (0.25W)
  74153 Dual 4:1 MUX: 74153 Dual 4:1 Multiplexor
  7404 Hex Inverter: 74XX04 Hex Inverter, Modified by Zuofu Cheng (Aug 2020)
  74157 Quad 2:1 MUX: 74157 Quad 2:1 Multiplexor
