# Fritzing sketch lab3 (saved by Fritzing 0.9.4)
breadboards: 3

parts:
  D1 = LED_BARGRAPH_10 [package=led_bargaph_10]
  D2 = LED_BARGRAPH_10 [package=led_bargaph_10]
  D3 = LED_BARGRAPH_10 [package=led_bargaph_10]
  D4 = LED_BARGRAPH_10 [package=led_bargaph_10]
  SW1 = DIP Switch 8 Position [package=dipswitch-08]
  U1 = 74194 4 Bit Bi-Directional Shift Register [part_number=74194 package="DIP16 [THT]"]
  U2 = 74194 4 Bit Bi-Directional Shift Register [part_number=74194 package="DIP16 [THT]"]
  U3 = 7486 4 x 2 Input XOR Gate [part_number=7486 package="DIP (Dual Inline) [THT]"]
  U5 = 74153 Dual 4:1 MUX [part_number=74153 package="DIP16 [THT]"]
  U7 = 7474 Dual Positive Edge Triggered D Flip Flop [part_number=7474 package="DIP (Dual Inline) [THT]"]
  U9 = 7404 Hex Inverter [part_number=7404 package=dil14]
  U10 = 7410 3 x 3 Input NAND Gate [part_number=7410 package="DIP (Dual Inline) [THT]"]
  U11 = 7400 4 x 2 Input NAND Gate [part_number=7400 package="DIP (Dual Inline) [THT]"]
  JP1 = Header 11 [package=1x11_smd_no_holes]
  U12 = 74153 Dual 4:1 MUX [part_number=74153 package="DIP16 [THT]"]
  R1 = 1kΩ Resistor [package=THT]
  R3 = 1kΩ Resistor [package=THT]
  R4 = 1kΩ Resistor [package=THT]
  R5 = 1kΩ Resistor [package=THT]
  R6 = 1kΩ Resistor [package=THT]
  R7 = 1kΩ Resistor [package=THT]
  R8 = 1kΩ Resistor [package=THT]
  R10 = 1kΩ Resistor [package=THT]
  R11 = 1kΩ Resistor [package=THT]
  R12 = 1kΩ Resistor [package=THT]
  R13 = 1kΩ Resistor [package=THT]
  R14 = 1kΩ Resistor [package=THT]
  R15 = 1kΩ Resistor [package=THT]
  R16 = 1kΩ Resistor [package=THT]
  R17 = 1kΩ Resistor [package=THT]
  R18 = 1kΩ Resistor [package=THT]
  U14 = 7474 Dual Positive Edge Triggered D Flip Flop [part_number=7474 package="DIP (Dual Inline) [THT]"]
  U15 = 7402 4 x 2 Input NOR Gate [part_number=7402 package="DIP (Dual Inline) [THT]"]

nets:
  N1: D1.C_A, U1.15
  N2: D1.D_A, U1.14
  N3: D1.E_A, U1.13
  N4: D1.F_A, U1.12, U3.Q2, U11.A4, U12.D0, U12.C1, U12.A1, U15.Q4
  N5: D1.F_C, R8.Pin_1
  N6: D1.E_C, R7.Pin_1
  N7: D1.D_C, R6.Pin_1
  N8: D1.C_C, R5.Pin_1
  N9: D2.B_A, U2.15
  N10: D2.C_A, U2.14
  N11: D2.D_A, U2.13, U12.A0, U12.B0, U12.D1
  N12: D2.E_A, U2.12, U3.A2, U11.Q4, U15.A4
  N13: D2.E_C, R13.Pin_1
  N14: D2.D_C, R11.Pin_1
  N15: D2.C_C, R10.Pin_1
  N16: D2.B_C, R12.Pin_1
  N17: D3.D_C, SW1.13, U1.6, U2.6, R4.Pin_1
  N18: D3.C_C, SW1.14, U1.5, U2.5, R3.Pin_1
  N19: D3.B_C, SW1.15, U1.4, U2.4, R14.Pin_1
  N20: D3.A_C, SW1.16, U1.3, U2.3, R1.Pin_1
  N21: D4.B_A, U2.10, U9.3Y
  N22: D4.C_A, U2.9, JP1.2, U15.B1
  N23: D4.D_A, U1.9, U9.6Y
  N24: D4.E_A, U1.10, JP1.3, U15.Q2
  N25: D4.E_C, R18.Pin_1
  N26: D4.D_C, R17.Pin_1
  N27: D4.C_C, R16.Pin_1
  N28: D4.B_C, R15.Pin_1
  GND: SW1.1, SW1.2, SW1.3, SW1.4, U1.GND, U2.1, U2.GND, U3.GND, U5.G0, U5.GND, U5.S1, U7.GND, U9.GND, U10.GND, U11.GND, JP1.5, U12.G1, U12.G0, U12.GND, R5.Pin_0, R6.Pin_0, R7.Pin_0, R8.Pin_0, R10.Pin_0, R11.Pin_0, R12.Pin_0, R13.Pin_0, R15.Pin_0, R16.Pin_0, R17.Pin_0, R18.Pin_0, U14.GND, U15.GND
  VDD: U1.1, U1.VCC, U2.VCC, U3.VDD, U5.D0, U5.VCC, U7.A1, U7.Q2, U7.VDD, U9.VCC, U10.VDD, U11.VDD, U12.VCC, R1.Pin_0, R3.Pin_0, R4.Pin_0, R14.Pin_0, U14.A1, U14.Q2, U14.Q3, U14.B4, U14.VDD, U15.VDD
  N29: U1.2, U12.Y1
  N30: U1.11, U2.11, U7.Q1, JP1.9, U14.Q1, U14.Q4
  N31: U2.2, U12.Y0
  N32: U3.A1, U7.A2, U11.Q2
  N33: U3.B1, U14.A3
  N34: U3.Q1, U7.B1
  N35: U3.B2, U5.C0
  N36: U3.A3, U5.Y0
  N37: U3.B3, JP1.6
  N38: U3.Q3, U12.C0, U12.B1
  N39: U5.A0, U9.5A, U11.B4
  N40: U5.B0, U15.B4
  N41: U5.S0, JP1.4
  N42: U7.B2, U10.A2, U10.B4
  N43: U9.1A, U11.A1, JP1.1
  N44: U9.1Y, U10.A1
  N45: U9.2A, U10.B2
  N46: U9.2Y, U15.A1, U15.A2
  N47: U9.3A, U15.Q1
  N48: U9.6A, U15.B2
  N49: U10.B1, U11.B1, U14.B2
  N50: U10.Q1, U11.A2, U14.B3
  N51: U10.Q2, U11.Q1, U11.B3
  N52: U10.A4, U14.B1
  N53: U11.B2, U11.A3
  N54: U11.Q3, U14.A4
  N55: JP1.7, U12.S0
  N56: JP1.8, U12.S1

custom parts:
  74153 Dual 4:1 MUX: 74153 Dual 4:1 Multiplexor
  7404 Hex Inverter: 74XX04 Hex Inverter, Modified by Zuofu Cheng (Aug 2020)
  7410 3 x 3 Input NAND Gate: 7410 3 x 2 Input NAND Gate
  1kΩ Resistor: A generic resistor (0.25W)
